// Logisim project Assignment2_Final_Laman_Panakhova_391 (1).circ as structural Verilog: 1 circuit, main circuit main
module main (
);

  wire and_1_out, and_2_out, and_3_out, and_4_out, and_5_out, and_6_out, and_7_out, and_8_out, and_9_out,
       and_10_out, and_11_out, and_12_out, clock_1_out, d_ff_1_qn, j_k_ff_1_qn, not_1_out, not_2_out,
       not_3_out, not_4_out, or_1_out, or_2_out, or_3_out, or_4_out, or_5_out, t_ff_1_qn, xor_1_out,
       xor_2_out, xor_3_out;
  wire [2:0] t_ff_1_q, t_ff_4_q;

  not not_1 (not_1_out, and_12_out);
  and and_1 (and_1_out, t_ff_1_q[2], not_1_out);
  and and_2 (and_2_out, d_ff_1_qn, and_12_out);
  and and_3 (and_3_out, t_ff_1_q[2], j_k_ff_1_qn);
  and and_4 (and_4_out, not_1_out, t_ff_4_q[1], t_ff_4_q[0]);
  and and_5 (and_5_out, and_12_out, t_ff_4_q[2]);
  and and_6 (and_6_out, not_1_out, t_ff_4_q[0]);
  and and_7 (and_7_out, t_ff_4_q[1], t_ff_4_q[0]);
  and and_8 (and_8_out, and_12_out, t_ff_4_q[1]);
  or or_1 (or_1_out, and_1_out, and_2_out, and_3_out);
  and and_9 (and_9_out, and_2_out, t_ff_1_q[0]);
  and and_10 (and_10_out, and_12_out, t_ff_1_q[2], t_ff_1_qn);
  and and_11 (and_11_out, and_12_out, t_ff_1_q[0]);
  or or_2 (or_2_out, and_6_out, and_7_out, and_8_out);
  or or_3 (or_3_out, and_10_out, and_11_out);
  Clock clock_1 (.out(clock_1_out));
  or or_4 (or_4_out, and_4_out, and_5_out);
  or or_5 (or_5_out, t_ff_4_q[0], not_1_out);
  D_Flip_Flop d_ff_1 (.clk(clock_1_out), .D(or_1_out), .Q(t_ff_1_q[2]), .Qn(d_ff_1_qn));  // open: preset, en, reset
  J_K_Flip_Flop j_k_ff_1 (
    .J(and_12_out), .clk(clock_1_out), .K(and_9_out), .Q(t_ff_1_q[1]), .Qn(j_k_ff_1_qn));  // open: preset, en, reset
  T_Flip_Flop t_ff_1 (.clk(clock_1_out), .T(or_3_out), .Q(t_ff_1_q[0]), .Qn(t_ff_1_qn));  // open: preset, reset, en
  T_Flip_Flop t_ff_2 (.clk(clock_1_out), .T(or_4_out), .Q(t_ff_4_q[2]));  // open: Qn, preset, reset, en
  T_Flip_Flop t_ff_3 (.clk(clock_1_out), .T(or_2_out), .Q(t_ff_4_q[1]));  // open: Qn, preset, reset, en
  T_Flip_Flop t_ff_4 (.clk(clock_1_out), .T(or_5_out), .Q(t_ff_4_q[0]));  // open: Qn, preset, reset, en
  Hex_Digit_Display hex_digit_display_1 (.value({1'b0, t_ff_1_q}));  // open: dp
  Hex_Digit_Display hex_digit_display_2 (.value({1'b0, t_ff_4_q}));  // open: dp
  xor xor_1 (xor_1_out, t_ff_1_q[2], t_ff_4_q[2]);
  xor xor_2 (xor_2_out, t_ff_1_q[1], t_ff_4_q[1]);
  xor xor_3 (xor_3_out, t_ff_1_q[0], t_ff_4_q[0]);
  not not_2 (not_2_out, xor_1_out);
  not not_3 (not_3_out, xor_2_out);
  not not_4 (not_4_out, xor_3_out);
  and and_12 (and_12_out, not_2_out, not_3_out, not_4_out);
endmodule
