// Logisim project Final.circ as structural Verilog: 1 circuit, main circuit main
module main (
);

  wire _1_out, _2_out, _3_out, _4_out, _5_out, _6_out, _7_out, and_1_out, and_2_out, and_3_out, and_4_out,
       and_5_out, and_6_out, and_7_out, not_1_out, not_2_out, not_3_out, or_1_out, or_2_out, or_3_out,
       or_4_out, or_5_out, or_6_out;
  wire [2:0] priority_encoder_1_out;

  Button _1 (.out(_1_out));
  Button _2 (.out(_2_out));
  Button _3 (.out(_3_out));
  Button _4 (.out(_4_out));
  Button _5 (.out(_5_out));
  Button _6 (.out(_6_out));
  Button _7 (.out(_7_out));
  Priority_Encoder priority_encoder_1 (
    .in1(_1_out), .in2(_2_out), .in3(_3_out), .in4(_4_out), .in5(_5_out), .in6(_6_out), .in7(_7_out),
    .out(priority_encoder_1_out));  // open: in0, en_in, gs, en_out
  not not_1 (not_1_out, priority_encoder_1_out[0]);
  not not_2 (not_2_out, priority_encoder_1_out[1]);
  not not_3 (not_3_out, priority_encoder_1_out[2]);
  and and_1 (and_1_out, priority_encoder_1_out[2], not_1_out);
  and and_2 (and_2_out, priority_encoder_1_out[1], not_1_out);
  and and_3 (and_3_out, priority_encoder_1_out[2], priority_encoder_1_out[1]);
  and and_4 (and_4_out, priority_encoder_1_out[2], not_2_out);
  and and_5 (and_5_out, priority_encoder_1_out[1], priority_encoder_1_out[0]);
  and and_6 (and_6_out, not_3_out, priority_encoder_1_out[1]);
  and and_7 (and_7_out, not_3_out, not_2_out, priority_encoder_1_out[0]);
  or or_1 (or_1_out, priority_encoder_1_out[2], priority_encoder_1_out[1], priority_encoder_1_out[0]);
  or or_2 (or_2_out, and_1_out, and_3_out, and_2_out, and_7_out);
  or or_3 (or_3_out, priority_encoder_1_out[2], priority_encoder_1_out[1]);
  or or_4 (or_4_out, and_1_out, priority_encoder_1_out[1]);
  or or_5 (or_5_out, and_4_out, and_5_out, and_6_out);
  or or_6 (or_6_out, and_1_out, and_2_out, and_3_out);
  _7_Segment_Display u_7_segment_display_1 (
    .g(or_3_out), .f(or_2_out), .a(or_4_out), .b(or_6_out), .e(or_1_out), .d(and_7_out), .c(or_5_out));  // open: dp

  // Notes on the sheet:
  //   a
  //   b
  //   c
  //   x6
  //   x7
  //   x1
  //   x4
  //   x5
  //   x2
  //   x3
endmodule
